// Logisim project Circuito_Codigo_Morse.circ as structural Verilog: 1 circuit, main circuit Codigo_Morse
module Codigo_Morse (
  input  A,
  input  B,
  input  C,
  input  D
);

  wire and_1_out, and_2_out, and_3_out, and_4_out, and_5_out, and_6_out, and_7_out, and_8_out, and_9_out,
       and_10_out, not_1_out, not_2_out, not_3_out, not_4_out, not_5_out, or_1_out, or_2_out, or_3_out,
       or_4_out, or_5_out;

  and and_1 (and_1_out, ~A, ~C, D);  // AND_Gate
  and and_2 (and_2_out, ~B, C);  // AND_Gate
  or or_1 (or_1_out, and_1_out, and_2_out, and_3_out);
  and and_3 (and_3_out, B, ~C);  // AND_Gate
  not not_1 (not_1_out, or_1_out);
  not not_2 (not_2_out, or_2_out);
  and and_4 (and_4_out, B, ~C);  // AND_Gate
  _7_Segment_Display u_7_segment_display_1 (.d(not_2_out), .dp(or_2_out));  // open: g, f, a, b, e, c
  _7_Segment_Display u_7_segment_display_2 (.d(not_1_out), .dp(or_1_out));  // open: g, f, a, b, e, c
  and and_5 (and_5_out, ~B, C);  // AND_Gate
  and and_6 (and_6_out, C, ~D);  // AND_Gate
  or or_2 (or_2_out, and_4_out, and_5_out, and_6_out);
  _7_Segment_Display u_7_segment_display_3 (.d(not_4_out), .dp(or_4_out));  // open: g, f, a, b, e, c
  _7_Segment_Display u_7_segment_display_4 (.d(not_3_out), .dp(or_3_out));  // open: g, f, a, b, e, c
  not not_3 (not_3_out, or_3_out);
  or or_3 (or_3_out, B, and_7_out);
  _7_Segment_Display u_7_segment_display_5 (.d(not_5_out), .dp(or_5_out));  // open: g, f, a, b, e, c
  and and_7 (and_7_out, C, D);
  not not_4 (not_4_out, or_4_out);
  and and_8 (and_8_out, A, ~C, ~D);  // AND_Gate
  or or_4 (or_4_out, B, and_8_out);
  not not_5 (not_5_out, or_5_out);
  and and_9 (and_9_out, B, C);
  or or_5 (or_5_out, and_9_out, A, and_10_out);
  and and_10 (and_10_out, B, D);

  // Notes on the sheet:
  //   d5
  //   d4
  //   d2
  //   d3
  //   d1
endmodule
